// Logisim project cache.circ as structural Verilog: 1 circuit, main circuit main
module main (
  input  Clock,
  input  [31:0] WriteData,
  input  [31:0] Address,
  output [31:0] ReadData,
  output HIT,
  output [31:0] AddressOut
);

  wire and_1_out, and_2_out, and_3_out, and_4_out, and_5_out, and_6_out, and_7_out, and_8_out,
       comparator_2_eq, comparator_4_eq, comparator_6_eq, comparator_8_eq, or_1_out, or_2_out, or_3_out,
       or_4_out, Select_0, Select_1, Select_2, Select_3, Select_4;
  wire [11:0] B0, B1, B2, B3, B4, B5, B6, B7;
  wire [31:0] multiplexer_1_out, multiplexer_2_out, multiplexer_3_out, multiplexer_4_out, multiplexer_5_out,
       multiplexer_6_out, multiplexer_7_out, multiplexer_8_out, multiplexer_9_out, multiplexer_10_out,
       multiplexer_12_out, W0, W1, W2, W3, W4, W5, W6, W7, W8, W9, W10, W11, W12, W13, W14, W15, W16, W17,
       W18, W19, W20, W21, W22, W23, W24, W25, W26, W27, W28, W29, W30, W31;

  Register #(.width(12)) register_1 (.Q(B0));  // open: D, en, clk, clr
  Register #(.width(12)) register_2 (.Q(B1));  // open: D, en, clk, clr
  Register #(.width(12)) register_3 (.Q(B2));  // open: D, en, clk, clr
  Register #(.width(12)) register_4 (.Q(B3));  // open: D, en, clk, clr
  Register #(.width(12)) register_5 (.Q(B4));  // open: D, en, clk, clr
  Register #(.width(12)) register_6 (.Q(B5));  // open: D, en, clk, clr
  Register #(.width(12)) register_7 (.Q(B6));  // open: D, en, clk, clr
  Register #(.width(12)) register_8 (.Q(B7));  // open: D, en, clk, clr
  Register #(.width(32)) register_9 (.D(WriteData), .clk(Clock), .Q(W0));  // open: en, clr
  Register #(.width(32)) register_10 (.D(WriteData), .clk(Clock), .Q(W4));  // open: en, clr
  Register #(.width(32)) register_11 (.D(WriteData), .clk(Clock), .Q(W8));  // open: en, clr
  Register #(.width(32)) register_12 (.D(WriteData), .clk(Clock), .Q(W12));  // open: en, clr
  Register #(.width(32)) register_13 (.D(WriteData), .clk(Clock), .Q(W16));  // open: en, clr
  Register #(.width(32)) register_14 (.D(WriteData), .clk(Clock), .Q(W20));  // open: en, clr
  Register #(.width(32)) register_15 (.D(WriteData), .clk(Clock), .Q(W24));  // open: en, clr
  Register #(.width(32)) register_16 (.D(WriteData), .clk(Clock), .Q(W28));  // open: en, clr
  Register #(.width(32)) register_17 (.D(WriteData), .clk(Clock), .Q(W1));  // open: en, clr
  Register #(.width(32)) register_18 (.D(WriteData), .clk(Clock), .Q(W5));  // open: en, clr
  Register #(.width(32)) register_19 (.D(WriteData), .clk(Clock), .Q(W9));  // open: en, clr
  Register #(.width(32)) register_20 (.D(WriteData), .clk(Clock), .Q(W13));  // open: en, clr
  Register #(.width(32)) register_21 (.D(WriteData), .clk(Clock), .Q(W17));  // open: en, clr
  Register #(.width(32)) register_22 (.D(WriteData), .clk(Clock), .Q(W21));  // open: en, clr
  Register #(.width(32)) register_23 (.D(WriteData), .clk(Clock), .Q(W25));  // open: en, clr
  Register #(.width(32)) register_24 (.D(WriteData), .clk(Clock), .Q(W29));  // open: en, clr
  Register #(.width(32)) register_25 (.D(WriteData), .clk(Clock), .Q(W2));  // open: en, clr
  Register #(.width(32)) register_26 (.D(WriteData), .clk(Clock), .Q(W6));  // open: en, clr
  Register #(.width(32)) register_27 (.D(WriteData), .clk(Clock), .Q(W10));  // open: en, clr
  Register #(.width(32)) register_28 (.D(WriteData), .clk(Clock), .Q(W14));  // open: en, clr
  Register #(.width(32)) register_29 (.D(WriteData), .clk(Clock), .Q(W18));  // open: en, clr
  Register #(.width(32)) register_30 (.D(WriteData), .clk(Clock), .Q(W22));  // open: en, clr
  Register #(.width(32)) register_31 (.D(WriteData), .clk(Clock), .Q(W26));  // open: en, clr
  Register #(.width(32)) register_32 (.D(WriteData), .clk(Clock), .Q(W30));  // open: en, clr
  Register #(.width(32)) register_33 (.D(WriteData), .clk(Clock), .Q(W3));  // open: en, clr
  Register #(.width(32)) register_34 (.D(WriteData), .clk(Clock), .Q(W7));  // open: en, clr
  Register #(.width(32)) register_35 (.D(WriteData), .clk(Clock), .Q(W11));  // open: en, clr
  Register #(.width(32)) register_36 (.D(WriteData), .clk(Clock), .Q(W15));  // open: en, clr
  Register #(.width(32)) register_37 (.D(WriteData), .clk(Clock), .Q(W19));  // open: en, clr
  Register #(.width(32)) register_38 (.D(WriteData), .clk(Clock), .Q(W23));  // open: en, clr
  Register #(.width(32)) register_39 (.D(WriteData), .clk(Clock), .Q(W27));  // open: en, clr
  Register #(.width(32)) register_40 (.D(WriteData), .clk(Clock), .Q(W31));  // open: en, clr
  Multiplexer #(.select(2), .width(32)) multiplexer_1 (
    .in0(W0), .in1(W1), .in2(W2), .in3(W3), .out(multiplexer_1_out), .sel(Address[3:2]));
  Multiplexer #(.select(2), .width(32)) multiplexer_2 (
    .in0(W4), .in1(W5), .in2(W6), .in3(W7), .out(multiplexer_2_out), .sel(Address[3:2]));
  Multiplexer #(.select(2), .width(32)) multiplexer_3 (
    .in0(W8), .in1(W9), .in2(W10), .in3(W11), .out(multiplexer_3_out), .sel(Address[3:2]));
  Multiplexer #(.select(2), .width(32)) multiplexer_4 (
    .in0(W12), .in1(W13), .in2(W14), .in3(W15), .out(multiplexer_4_out), .sel(Address[3:2]));
  Multiplexer #(.select(2), .width(32)) multiplexer_5 (
    .in0(W16), .in1(W17), .in2(W18), .in3(W19), .out(multiplexer_5_out), .sel(Address[3:2]));
  Multiplexer #(.select(2), .width(32)) multiplexer_6 (
    .in0(W20), .in1(W21), .in2(W22), .in3(W23), .out(multiplexer_6_out), .sel(Address[3:2]));
  Multiplexer #(.select(2), .width(32)) multiplexer_7 (
    .in0(W24), .in1(W25), .in2(W26), .in3(W27), .out(multiplexer_7_out), .sel(Address[3:2]));
  Multiplexer #(.select(2), .width(32)) multiplexer_8 (
    .in0(W28), .in1(W29), .in2(W30), .in3(W31), .out(multiplexer_8_out), .sel(Address[3:2]));
  Multiplexer #(.width(32)) multiplexer_9 (
    .in0(multiplexer_1_out), .in1(multiplexer_2_out), .out(multiplexer_9_out), .sel(Select_0));
  Multiplexer #(.width(32)) multiplexer_10 (
    .in0(multiplexer_3_out), .in1(multiplexer_4_out), .out(multiplexer_10_out), .sel(Select_1));
  Multiplexer #(.width(32)) multiplexer_11 (
    .in0(multiplexer_5_out), .in1(multiplexer_6_out), .out(multiplexer_10_out), .sel(Select_2));
  Multiplexer #(.width(32)) multiplexer_12 (
    .in0(multiplexer_7_out), .in1(multiplexer_8_out), .out(multiplexer_12_out), .sel(Select_3));
  Multiplexer #(.select(2), .width(32)) multiplexer_13 (
    .in0(multiplexer_9_out), .in1(multiplexer_10_out), .in2(multiplexer_10_out), .in3(multiplexer_12_out),
    .out(ReadData), .sel(Address[5:4]));
  Comparator #(.width(10)) comparator_1 (.a(B1[9:0]), .b(Address[15:6]), .eq(Select_0));  // open: gt, lt
  Comparator #(.width(10)) comparator_2 (.a(B0[9:0]), .b(Address[15:6]), .eq(comparator_2_eq));  // open: gt, lt
  and and_1 (and_1_out, B1[10], Select_0);
  and and_2 (and_2_out, B0[10], comparator_2_eq);
  or or_1 (or_1_out, and_1_out, and_2_out);
  Comparator #(.width(10)) comparator_3 (.a(B3[9:0]), .b(Address[15:6]), .eq(Select_1));  // open: gt, lt
  Comparator #(.width(10)) comparator_4 (.a(B2[9:0]), .b(Address[15:6]), .eq(comparator_4_eq));  // open: gt, lt
  and and_3 (and_3_out, B3[10], Select_1);
  and and_4 (and_4_out, B2[10], comparator_4_eq);
  Multiplexer #(.select(2)) multiplexer_14 (
    .in0(or_1_out), .in1(or_2_out), .in2(or_3_out), .in3(or_4_out), .out(HIT), .sel(Address[5:4]));
  or or_2 (or_2_out, and_3_out, and_4_out);
  Comparator #(.width(10)) comparator_5 (.a(B5[9:0]), .b(Address[15:6]), .eq(Select_2));  // open: gt, lt
  Comparator #(.width(10)) comparator_6 (.a(B4[9:0]), .b(Address[15:6]), .eq(comparator_6_eq));  // open: gt, lt
  and and_5 (and_5_out, B5[10], Select_2);
  or or_3 (or_3_out, and_5_out, and_6_out);
  and and_6 (and_6_out, B4[10], comparator_6_eq);
  Comparator #(.width(10)) comparator_7 (.a(B7[9:0]), .b(Address[15:6]), .eq(Select_4));  // open: gt, lt
  Comparator #(.width(10)) comparator_8 (.a(B6[9:0]), .b(Address[15:6]), .eq(comparator_8_eq));  // open: gt, lt
  and and_7 (and_7_out, B7[10], Select_4);
  and and_8 (and_8_out, B6[10], comparator_8_eq);
  or or_4 (or_4_out, and_7_out, and_8_out);

  assign AddressOut = Address;

  // Other names for the same wires on the sheet: word[1:0] = Address[3:2]; Set[1:0] = Address[5:4];
  //   Tag[9:0] = Address[15:6]
endmodule
