// Logisim project cpu.circ as structural Verilog: 1 circuit, main circuit cpu
module cpu (
  input  Rest
);

  wire alu_1_zero, alucontroller_1_sh_amount, and_1_out, and_2_out, and_3_out, and_4_out, and_5_out, AO, BR,
       BR_EXMEM, cache_1_p5, cache_1_p8, clk, comparator_1_eq, comparator_2_eq, comparator_3_eq,
       controller_1_alusrc, controller_1_branch, controller_1_jump, controller_1_lb, controller_1_memtoreg,
       controller_1_regdst, controller_1_regwren, ex_mem_1_memtoregout, ex_mem_1_regdstout,
       ex_mem_1_regwrenout, id_ex_1_alusrcout, id_ex_1_sh_amountout, JO, Jump_EXMEM, Jump_WB, LB, memToReg,
       MTR, multiplexer_1_out, not_1_out, or_1_out, RD, RegDst_WB, RegWrEn_WB, RType, RType2, RW, Zero_EXMEM;
  wire [1:0] alu_1_result, undriven;
  wire [3:0] bit_extender_5_out, controller_1_memwrmask, ex_mem_1_memwritemaskout, id_ex_1_memwrmaskout,
       multiplexer_8_out, oneclockdelay_1_dataout_2, shifter_4_out;
  wire [4:0] alucontroller_1_alu_out, bit_extender_4_out, ex_mem_1_wridxout, id_ex_1_alu_outout,
       multiplexer_4_out, oneclockdelay_2_dataout_2, oneclockdelay_2_dataout_3, shifter_5_out, WrIdx,
       WrIdx_IDEX, WrIdx_WB;
  wire [5:0] oneclockdelay_2_dataout;
  wire [7:0] multiplexer_13_out;
  wire [25:16] oneclockdelay_2_dataout_4;
  wire [27:0] oneclockdelay_1_dataout;
  wire [31:0] adder_1_out, adder_2_out, AluRes_EXMEM, bit_extender_1_out, bit_extender_2_out,
       bit_extender_3_out, bit_extender_6_out, cache_1_p6, cache_1_p7, cache_1_p9, ex_mem_1_addresscacheout,
       id_ex_1_extendedbitsout, id_ex_1_extendedout, id_ex_1_readdata1out, id_ex_1_readdata2out,
       mem_wb_1_alures_wb, mem_wb_1_cachereadout, MemData, multiplexer_2_out, multiplexer_5_out,
       multiplexer_6_out, multiplexer_7_out, multiplexer_9_out, multiplexer_10_out, multiplexer_11_out,
       multiplexer_12_out, multiplexer_14_out, multiplexer_15_out, pc, regfile_1_p7, regfile_1_p8,
       shifter_1_out, shifter_2_out, shifter_3_out, shifter_6_out, signextend_1_extended, undriven_2,
       xor_1_out;
  wire [31:2] alu_1_result_2;
  wire [31:26] oneclockdelay_2_dataout_5;

  Multiplexer multiplexer_1 (.in0(1'b1), .in1(1'b0), .out(multiplexer_1_out), .sel(and_3_out));
  Multiplexer #(.width(32)) multiplexer_2 (
    .in0(multiplexer_11_out), .in1(AluRes_EXMEM), .out(multiplexer_2_out), .sel(and_4_out));
  Register #(.width(32)) u_PC (.D(multiplexer_2_out), .en(multiplexer_1_out), .clk(clk), .Q(pc), .clr(Rest));
  Clock u_Clk (.out(clk));
  Adder #(.width(32)) adder_1 (.a(32'h4), .b(pc), .out(adder_1_out));  // open: cin, cout
  mem mem_1 (.MemAddress(pc), .clk(clk));  // open: MemWriteMask, MemWriteData, MemReadData
  oneClockDelay oneclockdelay_1 (
    .DataIn(adder_1_out), .clk(clk), .DataOut({oneclockdelay_1_dataout_2, oneclockdelay_1_dataout}));
  oneClockDelay oneclockdelay_2 (
    .DataIn({32{1'b0}}), .clk(clk),
    .DataOut({oneclockdelay_2_dataout_5, oneclockdelay_2_dataout_4, oneclockdelay_2_dataout_3, oneclockdelay_2_dataout_2, oneclockdelay_2_dataout}));
  Multiplexer #(.width(5)) multiplexer_3 (
    .in0(oneclockdelay_2_dataout_4[20:16]), .in1(oneclockdelay_2_dataout_3), .out(WrIdx),
    .sel(controller_1_regdst));
  assign bit_extender_1_out = {{6{1'b0}}, {oneclockdelay_2_dataout_4, oneclockdelay_2_dataout_3, oneclockdelay_2_dataout_2, oneclockdelay_2_dataout}};  // Bit_Extender bit_extender_1
  and and_1 (and_1_out, Jump_WB, RegWrEn_WB);
  Multiplexer #(.width(5)) multiplexer_4 (.in0(WrIdx_WB), .in1({5{1'b1}}), .out(multiplexer_4_out), .sel(and_1_out));
  Multiplexer #(.width(32)) multiplexer_5 (
    .in0(multiplexer_15_out), .in1(pc), .out(multiplexer_5_out), .sel(and_1_out));
  Shifter #(.width(32)) shifter_1 (.in(bit_extender_1_out), .\dist (5'b00010), .out(shifter_1_out));
  assign bit_extender_2_out = {{28{1'b0}}, oneclockdelay_1_dataout_2};  // Bit_Extender bit_extender_2
  assign bit_extender_3_out = {{27{1'b0}}, oneclockdelay_2_dataout_2};  // Bit_Extender bit_extender_3
  Shifter #(.width(32)) shifter_2 (.in(bit_extender_2_out), .\dist (5'b11100), .out(shifter_2_out));
  assign xor_1_out = shifter_1_out ^ shifter_2_out;  // XOR_Gate xor_1, 32 bits wide
  Controller controller_1 (
    .Opcode(oneclockdelay_2_dataout_5), .RegDst(controller_1_regdst), .Branch(controller_1_branch),
    .Jump(controller_1_jump), .RegWrEn(controller_1_regwren), .AluSrc(controller_1_alusrc),
    .MemToReg(controller_1_memtoreg), .AluOpr(AO), .MemWrMask(controller_1_memwrmask), .LB(controller_1_lb));
  // regfile regfile_1: pin names not known; wires that end beside it: oneclockdelay_2_dataout_4[25:21], oneclockdelay_2_dataout_4[20:16], multiplexer_4_out, multiplexer_5_out, RegWrEn_WB, clk, regfile_1_p7, regfile_1_p8
  signExtend signextend_1 (
    .Immd({oneclockdelay_2_dataout_3, oneclockdelay_2_dataout_2, oneclockdelay_2_dataout}),
    .Extended(signextend_1_extended));
  AluController alucontroller_1 (
    .func(oneclockdelay_2_dataout), .opcode(oneclockdelay_2_dataout_5), .aluOperation(AO),
    .ALU_out(alucontroller_1_alu_out), .sh_amount(alucontroller_1_sh_amount));
  ID_EX id_ex_1 (
    .clk(clk), .RegDstIn(controller_1_regdst), .BranchIn(controller_1_branch), .JumpIn(controller_1_jump),
    .RegWrEnIn(controller_1_regwren), .AluSrcIn(controller_1_alusrc), .MemToRegIn(controller_1_memtoreg),
    .AluOprIn(AO), .MemWrMaskIn(controller_1_memwrmask), .LBIn(controller_1_lb), .ReadData1In(regfile_1_p7),
    .ReadData2In(regfile_1_p8), .extendedBitsIn(bit_extender_3_out), .ExtendedIn(signextend_1_extended),
    .ALu_outIn(alucontroller_1_alu_out), .sh_amountIn(alucontroller_1_sh_amount), .WrIdxIn(WrIdx),
    .RegDstOut(RD), .BranchOut(BR), .JumpOut(JO), .RegWrEnOut(RW), .AluSrcOut(id_ex_1_alusrcout),
    .MemToRegOut(MTR), .AluOprOut(RType), .MemWrMaskOut(id_ex_1_memwrmaskout), .LBOut(LB),
    .ReadData1Out(id_ex_1_readdata1out), .ReadData2Out(id_ex_1_readdata2out),
    .extendedBitsOut(id_ex_1_extendedbitsout), .ExtendedOut(id_ex_1_extendedout),
    .Alu_outOut(id_ex_1_alu_outout), .sh_amountOut(id_ex_1_sh_amountout), .WrIdxOut(WrIdx_IDEX));
  and and_2 (and_2_out, ~BR, id_ex_1_alusrcout);  // AND_Gate
  Multiplexer #(.width(32)) multiplexer_6 (
    .in0(id_ex_1_readdata1out), .in1(id_ex_1_extendedbitsout), .out(multiplexer_6_out),
    .sel(id_ex_1_sh_amountout));
  Shifter #(.width(32)) shifter_3 (.in(id_ex_1_extendedout), .\dist (5'b00010), .out(shifter_3_out));
  Multiplexer #(.width(32)) multiplexer_7 (
    .in0(id_ex_1_readdata2out), .in1(id_ex_1_extendedout), .out(multiplexer_7_out), .sel(and_2_out));
  assign bit_extender_4_out = {{3{1'b0}}, alu_1_result};  // Bit_Extender bit_extender_4
  Adder #(.width(32)) adder_2 (
    .a({oneclockdelay_1_dataout_2, oneclockdelay_1_dataout}), .b(shifter_3_out), .out(adder_2_out));  // open: cin, cout
  Comparator #(.width(4)) comparator_1 (.a(id_ex_1_memwrmaskout), .b(4'b0001), .eq(comparator_1_eq));  // open: gt, lt
  Shifter #(.width(4)) shifter_4 (.in(id_ex_1_memwrmaskout), .\dist (alu_1_result), .out(shifter_4_out));
  Shifter #(.width(5)) shifter_5 (.in(bit_extender_4_out), .\dist (3'b011), .out(shifter_5_out));
  and and_3 (and_3_out, RType2, Zero_EXMEM, comparator_2_eq);
  and and_4 (and_4_out, Zero_EXMEM, ~comparator_2_eq, RType2);  // AND_Gate
  Shifter #(.width(32)) shifter_6 (.in(id_ex_1_readdata2out), .\dist (shifter_5_out), .out(shifter_6_out));
  Multiplexer #(.width(4)) multiplexer_8 (
    .in0(id_ex_1_memwrmaskout), .in1(shifter_4_out), .out(multiplexer_8_out), .sel(comparator_1_eq));
  ALU alu_1 (
    .ReadData1(multiplexer_6_out), .ReadData2(multiplexer_7_out), .ControlBits(id_ex_1_alu_outout),
    .Result({alu_1_result_2, alu_1_result}), .Zero(alu_1_zero));
  Multiplexer #(.width(32)) multiplexer_9 (
    .in0({oneclockdelay_1_dataout_2, oneclockdelay_1_dataout}), .in1(adder_2_out), .out(multiplexer_9_out),
    .sel(and_5_out));
  and and_5 (and_5_out, BR_EXMEM, Zero_EXMEM);
  Multiplexer #(.width(32)) multiplexer_10 (
    .in0(id_ex_1_readdata2out), .in1(shifter_6_out), .out(multiplexer_10_out), .sel(comparator_1_eq));
  Multiplexer #(.width(32)) multiplexer_11 (
    .in0(xor_1_out), .in1(multiplexer_9_out), .out(multiplexer_11_out), .sel(not_1_out));
  not not_1 (not_1_out, Jump_EXMEM);
  Comparator #(.width(32)) comparator_2 (.a(AluRes_EXMEM), .b({32{1'b1}}), .eq(comparator_2_eq));  // open: gt, lt
  EX_MEM ex_mem_1 (
    .Clock(clk), .ResultIn({alu_1_result_2, alu_1_result}), .AddressCacheIn(multiplexer_10_out),
    .ZeroIn(alu_1_zero), .BranchIn(BR), .RtypeIn(RType), .JumpIn(JO), .MemToRegIn(MTR), .RegDstIn(RD),
    .RegWrEnIn(RW), .MemWriteMaskIn(multiplexer_8_out), .LBIn(LB), .WrIdxIn(WrIdx_IDEX),
    .ResultOut(AluRes_EXMEM), .AddressCacheOut(ex_mem_1_addresscacheout), .ZeroOut(Zero_EXMEM),
    .BranchOut(BR_EXMEM), .RtypeOut(RType2), .JumpOut(Jump_EXMEM), .MemToRegOut(ex_mem_1_memtoregout),
    .RegDstOut(ex_mem_1_regdstout), .RegWrEnOut(ex_mem_1_regwrenout),
    .MemWriteMaskOut(ex_mem_1_memwritemaskout), .WrIdxOut(ex_mem_1_wridxout));  // open: Freeze, LBOut
  Multiplexer #(.width(32)) multiplexer_12 (.in0(MemData), .in1(AluRes_EXMEM), .out(multiplexer_12_out));  // open: sel
  Comparator #(.width(4)) comparator_3 (
    .a(4'b1111), .b(ex_mem_1_memwritemaskout), .eq(comparator_3_eq));  // open: gt, lt
  or or_1 (or_1_out, cache_1_p5, comparator_3_eq);
  assign bit_extender_5_out = {{3{cache_1_p8}}, cache_1_p8};  // Bit_Extender bit_extender_5
  // Cache cache_1: pin names not known; wires that end beside it: clk, ex_mem_1_addresscacheout, or_1_out, multiplexer_12_out, cache_1_p5, cache_1_p6, cache_1_p7, cache_1_p8, cache_1_p9
  memDelayed memdelayed_1 (
    .MemAddress(cache_1_p7), .MemWriteMask(bit_extender_5_out), .MemWriteData(cache_1_p9), .clk(clk),
    .MemReadData(MemData));
  assign bit_extender_6_out = {{24{1'b1}}, multiplexer_13_out};  // Bit_Extender bit_extender_6
  Multiplexer #(.select(2), .width(8)) multiplexer_13 (
    .in0(undriven_2[7:0]), .in1(undriven_2[15:8]), .in2(undriven_2[23:16]), .in3(undriven_2[31:24]),
    .out(multiplexer_13_out), .sel(undriven));
  Multiplexer #(.width(32)) multiplexer_14 (
    .in0(undriven_2), .in1(bit_extender_6_out), .out(multiplexer_14_out), .sel(LB));
  MEM_WB mem_wb_1 (
    .Clock(clk), .CacheReadDataIn(cache_1_p6), .MemToRegIn(ex_mem_1_memtoregout), .JumpIn(Jump_EXMEM),
    .RegDstIn(ex_mem_1_regdstout), .RegWrEnIn(ex_mem_1_regwrenout), .ALU_RES(AluRes_EXMEM),
    .WrIdxIn(ex_mem_1_wridxout), .CacheReadOut(mem_wb_1_cachereadout), .MemToRegOut(memToReg),
    .JumpOut(Jump_WB), .RegDstOut(RegDst_WB), .RegWrEnOut(RegWrEn_WB), .AluRes_WB(mem_wb_1_alures_wb),
    .WrIdxOut(WrIdx_WB));
  Multiplexer #(.width(32)) multiplexer_15 (
    .in0(mem_wb_1_alures_wb), .in1(mem_wb_1_cachereadout), .out(multiplexer_15_out), .sel(memToReg));
endmodule
